// Logisim project program counter.circ as structural Verilog: 1 circuit, main circuit main
module main (
  input  in_1,
  output [31:0] out_2,
  output [31:0] out_3
);

  wire clock_1_out;
  wire [31:0] adder_1_out;

  Clock clock_1 (.out(clock_1_out));
  Register #(.width(32)) register_1 (.D(adder_1_out), .Q(out_2), .clk(clock_1_out), .clr(in_1));  // open: en
  Adder #(.width(32)) adder_1 (.a(out_2), .b(32'h4), .out(adder_1_out));  // open: cin, cout
  ROM #(.addrWidth(24), .dataWidth(32)) rom_1 (.addr(out_2[25:2]), .data(out_3));  // open: sel

  // Notes on the sheet:
  //   PC
  //   contents of rom_1 (hex, n*v repeats v):
  //   111 124 4124
endmodule
